# Fritzing sketch circuito (saved by Fritzing 0.9.0b)
breadboards: 1

parts:
  Componente1 = Arduino Uno (Rev3)
  R1 = Resistor [tolerance=±10% resistance=1k package=THT]
  LCD1 = LCD screen
  S1 = Round Pushbutton

nets:
  N1: Componente1.A4/SDA, LCD1.V0
  N2: Componente1.A5/SCL, LCD1.RS
  N3: Componente1.D3_PWM, S1.leg0
  5V: Componente1.5V, R1.Pin_1, LCD1.VDD
  GND: Componente1.GND, LCD1.VSS, S1.leg1
